# Fritzing sketch 555speaker (saved by Fritzing 0.9.2b)
breadboards: 1

parts:
  SP1 = SPEAKER [package=pcb_mount_speaker]
  U1 = 555 Timer [package="DIP8 [THT]"]
  C1 = Capacitor [part_number=105 package=cap-pth-small2]
  C2 = Capacitor [part_number=104 package=cap-pth-small2]
  VCC1 = Battery block 9V
  R1 = Resistor [tolerance=±5% resistance=2.2k package=THT]
  C3 = Electrolytic Capacitor [capacitance=1µF package="100 mil [THT, electrolytic]"]
  R2 = Resistor [tolerance=±5% resistance=10k package=THT]

nets:
  N1: SP1.+, C3.-
  GND: SP1.-, U1.Ground, C1.2, C2.2, VCC1.-
  N2: U1.Trigger, U1.Threshold, C2.1, R2.Pin_1
  N3: U1.Output, C3.+
  N4: U1.Reset, U1.Vcc_Supply_Voltage, VCC1.+, R1.Pin_1
  N5: U1.Control_Voltage, C1.1
  N6: U1.Discharge, R1.Pin_0, R2.Pin_0
