# Fritzing sketch clk_temp_lites (saved by Fritzing 0.9.2b)
breadboards: 1

parts:
  Raspberry_Pi1 = Raspberry Pi 2
  Part1 = Real Time Clock Module - DS1307 RTC Breakout Board
  LED3 = smd LED [color="Green (565nm)" package="0603 [SMD]"]
  LED4 = smd LED [color="White (4500K)" package="0603 [SMD]"]
  LED5 = smd LED [color="Yellow (595nm)" package="0603 [SMD]"]
  LED6 = smd LED [color="Red (633nm)" package="0603 [SMD]"]
  LED7 = smd LED [color="White (4500K)" package="0603 [SMD]"]
  R1 = Resistor [tolerance=±5% resistance=330 package="2512 [SMD]"]
  R2 = Resistor [tolerance=±5% resistance=330 package="2512 [SMD]"]
  R3 = Resistor [tolerance=±5% resistance=330 package="2512 [SMD]"]
  R4 = Resistor [tolerance=±5% resistance=330 package="2512 [SMD]"]
  R5 = Resistor [tolerance=±5% resistance=330 package="2512 [SMD]"]
  S4 = Momentary Switch [package=ksa_sealed_tac_switch]

nets:
  3V3: Raspberry_Pi1.3v3, Part1.5V
  N1: Raspberry_Pi1.GPIO2, Part1.SDA
  N2: Raspberry_Pi1.GPIO3, Part1.SCL
  N3: Raspberry_Pi1.GPIO4, Part1.GND, LED3.cathode, LED4.cathode, LED5.cathode, LED6.cathode, LED7.cathode, S4.3, S4.4
  N4: Raspberry_Pi1.GPIO13, S4.1, S4.2
  N5: Raspberry_Pi1.GPIO19, R4.Pin_0
  N6: Raspberry_Pi1.GPIO26, R3.Pin_0
  N7: Raspberry_Pi1.GPIO21, R1.Pin_0
  N8: Raspberry_Pi1.GPIO20, R2.Pin_0
  N9: Raspberry_Pi1.GPIO16, R5.Pin_0
  N10: LED3.anode, R2.Pin_1
  N11: LED4.anode, R1.Pin_1
  N12: LED5.anode, R3.Pin_1
  N13: LED6.anode, R4.Pin_1
  N14: LED7.anode, R5.Pin_1
