# Fritzing sketch delay (saved by Fritzing 0.9.2b)
breadboards: 1

parts:
  U1 = 555 Timer [package="SO8 [SMD]"]
  LED1 = LEDs [package=led10mm]
  R1 = Resistor [tolerance=±5% resistance=220k package=THT]
  R2 = Resistor [tolerance=±5% resistance=330 package=THT]
  D1 = Rectifier Diode [part_number=1N4148 package="300 mil [THT]"]
  V1 = DC Power [voltage=5]
  C1 = Tantalum Capacitor [capacitance=47µF package="100 mil [THT, tantalum]"]
  S1 = Pushbutton [package=THT]

nets:
  GND: U1.Pin_1, LED1.C, R1.Pin_1, D1.anode, V1.V-
  N1: U1.Pin_2, U1.Pin_6, R1.Pin_0, D1.cathode, C1.-
  N2: U1.Pin_3, R2.Pin_0
  N3: U1.Pin_4, U1.Pin_8, C1.+, S1.leg1
  N4: LED1.A, R2.Pin_1
  N5: V1.V+, S1.leg0

notes:
  Delay On with 555
  t(secs)=1.1*R1*C1/1000
  Where R is in KΩ and C is in μF
  delay time ~ 11.5s
