# Fritzing sketch delay_on (saved by Fritzing 0.9.2b)
breadboards: 1

parts:
  V1 = DC Power [voltage=5]
  R1 = Resistor [tolerance=±5% resistance=680k package=THT]
  D1 = Rectifier Diode [part_number=1N4148 package="300 mil [THT]"]
  D3 = Zener Diode [part_number=1N5226B breakdown_voltage=3.3V package="300 mil [THT]"]
  R2 = Resistor [tolerance=±5% resistance=330k package=THT]
  R3 = Resistor [tolerance=±5% resistance=10k package=THT]
  R4 = Resistor [tolerance=±5% resistance=1k package=THT]
  S1 = Pushbutton [package=THT]
  D2 = Rectifier Diode [part_number=1N4148 package="300 mil [THT]"]
  C1 = Electrolytic Capacitor [capacitance=47µF package="100 mil [THT, electrolytic]"]
  Q1 = NPN-Transistor [package="TO92 [THT]"]
  Q2 = PNP-Transistor [package="TO92 [THT]"]
  R5 = Resistor [tolerance=±5% resistance=330 package=THT]
  LED2 = LEDs [package=led10mm]

nets:
  N1: V1.V+, S1.leg0
  GND: V1.V-, R1.Pin_1, D1.anode, D3.anode, C1.-, LED2.C
  N2: R1.Pin_0, D2.cathode, C1.+
  N3: D1.cathode, Q2.C, R5.Pin_0
  N4: D3.cathode, Q1.E
  N5: R2.Pin_0, R4.Pin_0, S1.leg1, Q2.E
  N6: R2.Pin_1, D2.anode, Q1.B
  N7: R3.Pin_0, R4.Pin_1, Q2.B
  N8: R3.Pin_1, Q1.C
  N9: R5.Pin_1, LED2.A

notes:
  Output
  Delay On
