# Fritzing sketch latch_reset (saved by Fritzing 0.9.2b)
breadboards: 1

parts:
  U1 = 555 Timer [package="DIP8 [THT]"]
  R1 = Resistor [tolerance=±5% resistance=100k package=THT]
  R2 = Resistor [tolerance=±5% resistance=100k package=THT]
  R4 = Resistor [tolerance=±5% resistance=3.3k package=THT]
  R3 = Resistor [tolerance=±5% resistance=330 package=THT]
  C1 = Ceramic Capacitor [capacitance=100nF part_number=104 package="100 mil [THT, multilayer]"]
  Q1 = NPN-Transistor [package="TO92 [THT]"]
  LED1 = LEDs [package=led10mm]
  V1 = DC Power [voltage=5]
  Q2 = NPN-Transistor [package="TO92 [THT]"]
  R6 = Resistor [tolerance=±5% resistance=3.3k package=THT]
  R5 = Resistor [tolerance=±5% resistance=2.2k package=THT]
  R7 = Resistor [tolerance=±5% resistance=2.2k package=THT]

nets:
  GND: U1.Ground, U1.Threshold, C1.0, Q1.E, LED1.C, V1.V-, Q2.E, R5.Pin_1, R7.Pin_1
  N1: U1.Trigger, R1.Pin_1, Q1.C
  N2: U1.Output, R3.Pin_0
  N3: U1.Reset, R2.Pin_1, C1.1, Q2.C
  N4: U1.Vcc_Supply_Voltage, R1.Pin_0, R2.Pin_0, V1.V+
  5V: R4.Pin_0, R6.Pin_0
  N5: R4.Pin_1, Q1.B, R5.Pin_0
  N6: R3.Pin_1, LED1.A
  N7: Q2.B, R6.Pin_1, R7.Pin_0

notes:
  Output
  Reset Signal
  Set Signal
  Latch with Reset
