# Fritzing sketch latch_reset_sink (saved by Fritzing 0.9.2b)
breadboards: 1

parts:
  U1 = 555 Timer [package="DIP8 [THT]"]
  R1 = Resistor [tolerance=±5% resistance=100k package=THT]
  R2 = Resistor [tolerance=±5% resistance=100k package=THT]
  R4 = Resistor [tolerance=±5% resistance=3.3k package=THT]
  R3 = Resistor [tolerance=±5% resistance=330 package=THT]
  C1 = Ceramic Capacitor [capacitance=100nF part_number=104 package="100 mil [THT, multilayer]"]
  LED1 = LEDs [package=led10mm]
  V1 = DC Power [voltage=5]
  Q2 = NPN-Transistor [package="TO92 [THT]"]
  R6 = Resistor [tolerance=±5% resistance=3.3k package=THT]
  R5 = Resistor [tolerance=±5% resistance=2.2k package=THT]
  R7 = Resistor [tolerance=±5% resistance=2.2k package=THT]
  Q3 = PNP-Transistor [package="TO92 [THT]"]

nets:
  GND: U1.Ground, U1.Trigger, U1.Threshold, R1.Pin_1, R4.Pin_1, C1.0, V1.V-, Q2.E, R7.Pin_1
  N1: U1.Output, R3.Pin_0
  N2: U1.Reset, R2.Pin_1, C1.1, Q2.C
  N3: U1.Vcc_Supply_Voltage, R2.Pin_0, LED1.A, V1.V+, R5.Pin_0, Q3.E
  N4: R1.Pin_0, Q3.C
  N5: R4.Pin_0, R5.Pin_1, Q3.B
  N6: R3.Pin_1, LED1.C
  N7: Q2.B, R6.Pin_1, R7.Pin_0
  5V: R6.Pin_0

notes:
  Output sink
  Reset Signal
  Set Signal
  Latch with Reset as Sink
