# Fritzing sketch latch_transistor (saved by Fritzing 0.9.2b)
breadboards: 1

parts:
  Q1 = PNP-Transistor [package="TO92 [THT]"]
  Q2 = NPN-Transistor [package="TO92 [THT]"]
  R1 = Resistor [tolerance=±5% resistance=100k package=THT]
  R2 = Resistor [tolerance=±5% resistance=10k package=THT]
  R3 = Resistor [tolerance=±5% resistance=27k package=THT]
  Reset = Pushbutton [package=THT]
  D1 = Rectifier Diode [part_number=1N4001 package="300 mil [THT]"]
  S1 = Pushbutton [package=THT]
  Reset_2 = Pushbutton [package=THT]
  NC_Switch = Pushbutton [package=THT]
  R4 = Resistor [tolerance=±5% resistance=1k package=THT]
  NO_Switch = Pushbutton [package=THT]
  R5 = Resistor [tolerance=±5% resistance=330 package=THT]
  LED1 = LEDs [package=led10mm]
  Q3 = PNP-Transistor [package="TO92 [THT]"]
  R6 = Resistor [tolerance=±5% resistance=2.2k package=THT]
  R7 = Resistor [tolerance=±5% resistance=3.3k package=THT]
  V1 = DC Power [voltage=5]
  C2 = Electrolytic Capacitor [capacitance=10µF package="100 mil [THT, electrolytic]"]

nets:
  N1: Q1.E, R2.Pin_1, Reset.leg0
  N2: Q1.B, Q2.C, Reset.leg1, R4.Pin_0, LED1.C, R7.Pin_1
  N3: Q1.C, Q2.B, R3.Pin_0, D1.cathode, Reset_2.leg0, C2.+
  GND: Q2.E, R3.Pin_1, Reset_2.leg1, NC_Switch.leg0, NO_Switch.leg0, V1.V-, C2.-
  N4: R1.Pin_0, R2.Pin_0, S1.leg1, R5.Pin_0, R6.Pin_0
  N5: R1.Pin_1, D1.anode, NC_Switch.leg1
  N6: S1.leg0, V1.V+
  N7: R4.Pin_1, NO_Switch.leg1
  N8: R5.Pin_1, LED1.A
  N9: Q3.B, R6.Pin_1, R7.Pin_0
