# Fritzing sketch piezo_speaker (saved by Fritzing 0.9.2b)
breadboards: 1

parts:
  U1 = 555 Timer [package="DIP8 [THT]"]
  J1 = Piezo Speaker
  R1 = Resistor [tolerance=±5% resistance=39k package=THT]
  R2 = Resistor [tolerance=±5% resistance=18k package=THT]
  Q1 = NPN-Transistor [package="TO92 [THT]"]
  C1 = Ceramic Capacitor [capacitance=4.7µF package="100 mil [THT, multilayer]"]
  R3 = Resistor [tolerance=±5% resistance=3.3k package=THT]
  V2 = DC Power [voltage=5]
  S1 = Pushbutton [package=THT]
  R4 = Resistor [tolerance=±5% resistance=2.2k package=THT]
  U2 = OP27 - Low Noise, Precision Op Amp [part_number=OP27]
  R5 = Resistor [tolerance=±5% resistance=3.3k package=THT]
  R6 = Resistor [tolerance=±5% resistance=10k package=THT]
  U3 = 555 Timer [package="DIP8 [THT]"]
  R7 = Resistor [tolerance=±5% resistance=10k package=THT]
  R8 = Resistor [tolerance=±5% resistance=10k package=THT]
  C2 = Ceramic Capacitor [capacitance=10nF package="100 mil [THT, multilayer]"]

nets:
  GND: U1.Ground, J1.pin2, Q1.E, V2.V-, R4.Pin_0, U2.+IN, U2.-V, U3.Ground, C2.0
  N1: U1.Trigger, U1.Threshold, R2.Pin_1, C1.1
  N2: U1.Output, R7.Pin_0
  N3: U1.Reset, U1.Vcc_Supply_Voltage, R1.Pin_0, S1.leg1, U2.V+, U3.Reset, U3.Vcc_Supply_Voltage
  N4: U1.Discharge, R1.Pin_1, R2.Pin_0
  N5: J1.pin1, U2.OUT, R6.Pin_1
  N6: Q1.B, R3.Pin_0, R4.Pin_1
  N7: Q1.C, C1.0
  5V: R3.Pin_1
  N8: V2.V+, S1.leg0
  N9: U2.-IN, R5.Pin_1, R6.Pin_0
  N10: R5.Pin_0, U3.Output
  N11: U3.Trigger, U3.Threshold, R8.Pin_1, C2.1
  N12: U3.Discharge, R7.Pin_1, R8.Pin_0

notes:
  On Signal
  Frequency output to Piezo speaker
