# Fritzing sketch sprinklelight (saved by Fritzing 0.9.2b)
perfboards: 1

parts:
  Raspberry_Pi1 = Raspberry Pi 2
  J6 = screw terminal, 5 pins
  J8 = screw terminal, 5 pins
  S8 = Pushbutton [package="[THT]"]
  S9 = Pushbutton [package="[THT]"]
  S10 = Pushbutton [package="[THT]"]
  S11 = Pushbutton [package="[THT]"]
  S12 = Pushbutton [package="[THT]"]
  S13 = Pushbutton [package="[THT]"]
  S14 = Pushbutton [package="[THT]"]
  S15 = Pushbutton [package="[THT]"]
  S16 = Pushbutton [package="[THT]"]
  S17 = Pushbutton [package="[THT]"]
  Part2 = Real Time Clock Module - DS1307 RTC Breakout Board
  S18 = Pushbutton [package="[THT]"]
  U11 = RELAY [package=relay-jzc]
  U12 = RELAY [package=relay-jzc]
  U13 = RELAY [package=relay-jzc]
  U14 = RELAY [package=relay-jzc]
  U15 = RELAY [package=relay-jzc]
  U16 = RELAY [package=relay-jzc]
  U17 = RELAY [package=relay-jzc]
  U18 = RELAY [package=relay-jzc]
  J9 = screw terminal, 10 pins
  J10 = screw terminal, 5 pins
  PIR1 = PIR sensor
  Part3 = Adafruit TSL2561 [part_number="Adafruit #439"]
  J11 = screw terminal, 5 pins

nets:
  3V3: Raspberry_Pi1.3v3, Part2.5V, PIR1.VDD, Part3.3.3V, J11.pin1
  N1: Raspberry_Pi1.GPIO2, Part2.SDA, Part3.SDA, J11.pin5
  N2: Raspberry_Pi1.GPIO3, Part2.SCL, Part3.SCL, J11.pin4
  N3: Raspberry_Pi1.GPIO4, U16.COIL1, J9.pin2
  GND: Raspberry_Pi1.GND, S8.Pin_1, S8.Pin_2, S9.Pin_1, S9.Pin_2, S10.Pin_1, S10.Pin_2, S11.Pin_1, S11.Pin_2, S12.Pin_1, S12.Pin_2, S13.Pin_3, S13.Pin_4, S14.Pin_3, S14.Pin_4, S15.Pin_3, S15.Pin_4, S16.Pin_1, S16.Pin_2, S17.Pin_1, S17.Pin_2, Part2.GND, S18.Pin_1, S18.Pin_2, U11.COIL2, U12.COIL2, U13.COIL2, U14.COIL2, U15.COIL2, U16.COIL2, U17.COIL2, U18.COIL2, J9.pin10, PIR1.GND, Part3.GND, J11.pin3
  N4: Raspberry_Pi1.GPIO17, U14.COIL1, J9.pin3
  N5: Raspberry_Pi1.GPIO27, U11.COIL1, J9.pin4
  N6: Raspberry_Pi1.GPIO22, U12.COIL1, J9.pin5
  N7: Raspberry_Pi1.GPIO11, J11.pin2
  N8: Raspberry_Pi1.GPIO5, S11.Pin_3, S11.Pin_4
  N9: Raspberry_Pi1.GPIO6, S10.Pin_3, S10.Pin_4
  N10: Raspberry_Pi1.GPIO13, S14.Pin_1, S14.Pin_2
  N11: Raspberry_Pi1.GPIO19, S15.Pin_1, S15.Pin_2
  N12: Raspberry_Pi1.GPIO26, S13.Pin_1, S13.Pin_2
  N13: Raspberry_Pi1.GPIO21, S16.Pin_3, S16.Pin_4
  N14: Raspberry_Pi1.GPIO20, S17.Pin_3, S17.Pin_4
  N15: Raspberry_Pi1.GPIO16, S8.Pin_3, S8.Pin_4
  N16: Raspberry_Pi1.GPIO12, S12.Pin_3, S12.Pin_4
  N17: Raspberry_Pi1.GPIO7, S9.Pin_3, S9.Pin_4
  N18: Raspberry_Pi1.GPIO8, S18.Pin_3, S18.Pin_4
  N19: Raspberry_Pi1.GPIO25, U18.COIL1, J9.pin9
  N20: Raspberry_Pi1.GPIO24, U15.COIL1, J9.pin8
  N21: Raspberry_Pi1.GPIO23, U13.COIL1, J9.pin7
  N22: Raspberry_Pi1.GPIO18, U17.COIL1, J9.pin6
  N23: Raspberry_Pi1.5V, J9.pin1
  N24: J6.pin1, U18.NO
  N25: J6.pin2, U15.NO
  N26: J6.pin3, U13.NO
  N27: J6.pin4, U17.NO
  N28: J6.pin5, U12.NO
  N29: J8.pin1, U11.MAIN, U12.MAIN, U13.MAIN, U15.MAIN, U17.MAIN, U18.MAIN
  N30: J8.pin2, U14.MAIN, U16.MAIN
  N31: J8.pin3, J8.pin4, J8.pin5
  N32: U11.NO, J10.pin1
  N33: U14.NO, J10.pin2
  N34: U16.NO, J10.pin3

custom parts:
  Adafruit TSL2561: The TSL2561 luminosity sensor is an advanced digital light sensor, ideal for use in a wide range of light situations. Compared to low cost CdS cells, this sensor is more precise, allowing for exact lux calculations and can be configured for different gain/timing ranges to detect light ranges from up to 0.1 - 40,000+ Lux on the fly. The best part of this sensor is that it contains both infrared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
